// Logisim project Full Adder.circ as structural Verilog: 12 circuits, main circuit Main
module Main (
  input  in_1,
  input  in_2,
  input  in_3,
  input  in_4,
  input  in_5,
  input  in_6,
  input  in_7,
  input  in_8,
  output out_9,
  output out_10,
  output out_11,
  output out_12,
  output out_13,
  output out_14
);

  Main_Arithmatic_Unit__Mag main_arithmatic_unit_mag_1 (
    .S0(in_7), .S1(in_8), .B2(in_1), .B1(in_2), .B0(in_3), .A2(in_4), .A1(in_5), .A0(in_6), .E_F(out_9),
    .sign(out_10), .X3(out_11), .X2(out_12), .X1(out_13), .X0(out_14));
endmodule

module Main_Arithmatic_Unit__Mag (
  input  B2,
  input  B1,
  input  B0,
  input  A2,
  input  A1,
  input  A0,
  input  S0,
  input  S1,
  output E_F,
  output sign,
  output X3,
  output X2,
  output X1,
  output X0
);

  wire n3_bit_adder_sub_1_overflow, n3_bit_adder_sub_1_s0, n3_bit_adder_sub_1_s1, n3_bit_adder_sub_1_s2,
       n3_bit_inverter_v1_0_1_x0_2, n3_bit_inverter_v1_0_1_x1_2, n3_bit_inverter_v1_0_1_x2_2,
       n3_bit_inverter_v1_0_2_x0_2, n3_bit_inverter_v1_0_2_x1_2, n3_bit_inverter_v1_0_2_x2_2,
       n3_bit_inverter_v2_0_1_x0_2, n3_bit_inverter_v2_0_1_x1_2, n3_bit_inverter_v2_0_1_x2_2,
       n3_bit_multiplier_v2_0_1_e_f, n3_bit_multiplier_v2_0_1_m0, n3_bit_multiplier_v2_0_1_m1,
       n3_bit_multiplier_v2_0_1_m2, n3_bit_multiplier_v2_0_1_m3, n3_bit_multiplier_v2_0_1_sign;

  _3_Bit_Multiplier_v2_0 u_3_bit_multiplier_v2_0_1 (
    .B2(B2), .A2(A2), .B1(B1), .B0(B0), .A1(A1), .A0(A0), .Sign(n3_bit_multiplier_v2_0_1_sign),
    .M3(n3_bit_multiplier_v2_0_1_m3), .M2(n3_bit_multiplier_v2_0_1_m2), .M1(n3_bit_multiplier_v2_0_1_m1),
    .M0(n3_bit_multiplier_v2_0_1_m0), .E_F(n3_bit_multiplier_v2_0_1_e_f));
  _2X5_Multiplexer u_2x5_multiplexer_1 (
    .S0(S1), .B4(n3_bit_multiplier_v2_0_1_sign), .B3(n3_bit_multiplier_v2_0_1_m3),
    .B2(n3_bit_multiplier_v2_0_1_m2), .B1(n3_bit_multiplier_v2_0_1_m1), .B0(n3_bit_multiplier_v2_0_1_m0),
    .A2(n3_bit_inverter_v2_0_1_x2_2), .A1(n3_bit_inverter_v2_0_1_x1_2), .A0(n3_bit_inverter_v2_0_1_x0_2),
    .X_2(sign), .X_3(X3), .X_4(X2), .X_5(X1), .X_6(X0), .EFA(n3_bit_adder_sub_1_overflow),
    .EFB(n3_bit_multiplier_v2_0_1_e_f), .X(E_F));
  _3_Bit_Inverter_v1_0 u_3_bit_inverter_v1_0_1 (
    .X2(B2), .X1(B1), .X0(B0), .X2_2(n3_bit_inverter_v1_0_1_x2_2), .X1_2(n3_bit_inverter_v1_0_1_x1_2),
    .X0_2(n3_bit_inverter_v1_0_1_x0_2));
  _3_Bit_Adder_Sub u_3_bit_adder_sub_1 (
    .A0(n3_bit_inverter_v1_0_2_x0_2), .A1(n3_bit_inverter_v1_0_2_x1_2), .A2(n3_bit_inverter_v1_0_2_x2_2),
    .B0(n3_bit_inverter_v1_0_1_x0_2), .B1(n3_bit_inverter_v1_0_1_x1_2), .B2(n3_bit_inverter_v1_0_1_x2_2),
    .S0(n3_bit_adder_sub_1_s0), .S1(n3_bit_adder_sub_1_s1), .S2(n3_bit_adder_sub_1_s2),
    .overflow(n3_bit_adder_sub_1_overflow), .M(S0));  // open: Carry
  _3_Bit_Inverter_v1_0 u_3_bit_inverter_v1_0_2 (
    .X2(A2), .X1(A1), .X0(A0), .X2_2(n3_bit_inverter_v1_0_2_x2_2), .X1_2(n3_bit_inverter_v1_0_2_x1_2),
    .X0_2(n3_bit_inverter_v1_0_2_x0_2));
  _3_Bit_Inverter_v2_0 u_3_bit_inverter_v2_0_1 (
    .X2(n3_bit_adder_sub_1_s2), .X1(n3_bit_adder_sub_1_s1), .X0(n3_bit_adder_sub_1_s0),
    .X2_2(n3_bit_inverter_v2_0_1_x2_2), .X1_2(n3_bit_inverter_v2_0_1_x1_2), .X0_2(n3_bit_inverter_v2_0_1_x0_2));
endmodule

module Main_Arithmatic_Unit__complements (
  input  B2,
  input  B1,
  input  B0,
  input  A2,
  input  A1,
  input  A0,
  input  S0,
  input  S1,
  output E_F,
  output X,
  output X_2,
  output X_3,
  output X_4,
  output X0
);

  wire n3_bit_adder_sub_1_overflow, n3_bit_adder_sub_1_s0, n3_bit_adder_sub_1_s1, n3_bit_adder_sub_1_s2,
       n3_bit_multiplier_v3_0_1_m, n3_bit_multiplier_v3_0_1_m0, n3_bit_multiplier_v3_0_1_m1,
       n3_bit_multiplier_v3_0_1_m2, n3_bit_multiplier_v3_0_1_overflow, n3_bit_multiplier_v3_0_1_sign;

  _3_Bit_Multiplier_v3_0 u_3_bit_multiplier_v3_0_1 (
    .B2(B2), .B1(B1), .B0(B0), .A2(A2), .A1(A1), .A0(A0), .Overflow(n3_bit_multiplier_v3_0_1_overflow),
    .Sign(n3_bit_multiplier_v3_0_1_sign), .M(n3_bit_multiplier_v3_0_1_m), .M2(n3_bit_multiplier_v3_0_1_m2),
    .M1(n3_bit_multiplier_v3_0_1_m1), .M0(n3_bit_multiplier_v3_0_1_m0));  // open: Carry
  or or_1 (E_F, n3_bit_multiplier_v3_0_1_overflow, n3_bit_adder_sub_1_overflow);
  _2X5_Multiplexer u_2x5_multiplexer_1 (
    .S0(S1), .B4(n3_bit_multiplier_v3_0_1_sign), .B3(n3_bit_multiplier_v3_0_1_m),
    .B2(n3_bit_multiplier_v3_0_1_m2), .B1(n3_bit_multiplier_v3_0_1_m1), .B0(n3_bit_multiplier_v3_0_1_m0),
    .A2(n3_bit_adder_sub_1_s2), .A1(n3_bit_adder_sub_1_s1), .A0(n3_bit_adder_sub_1_s0), .X_2(X), .X_3(X_2),
    .X_4(X_3), .X_5(X_4), .X_6(X0));  // open: EFA, EFB, X
  _3_Bit_Adder_Sub u_3_bit_adder_sub_1 (
    .A0(A0), .A1(A1), .A2(A2), .B0(B0), .B1(B1), .B2(B2), .S0(n3_bit_adder_sub_1_s0),
    .S1(n3_bit_adder_sub_1_s1), .S2(n3_bit_adder_sub_1_s2), .overflow(n3_bit_adder_sub_1_overflow), .M(S0));  // open: Carry
endmodule

module _3_Bit_Adder_Sub (
  input  M,
  input  A0,
  input  A1,
  input  A2,
  input  B0,
  input  B1,
  input  B2,
  output S0,
  output S1,
  output S2,
  output overflow,
  output Carry
);

  wire F_A_2_carry_2, F_A_carry_2, xor_1_out, xor_2_out, xor_3_out;

  xor xor_1 (xor_1_out, M, B0);
  xor xor_2 (xor_2_out, M, B1);
  xor xor_3 (xor_3_out, M, B2);
  Full_Adder F_A (.Carry(M), .X(A0), .Y(xor_1_out), .Sum(S0), .Carry_2(F_A_carry_2));
  Full_Adder F_A_2 (.Carry(F_A_carry_2), .X(A1), .Y(xor_2_out), .Sum(S1), .Carry_2(F_A_2_carry_2));
  Full_Adder F_A_3 (.Carry(F_A_2_carry_2), .X(A2), .Y(xor_3_out), .Sum(S2), .Carry_2(Carry));
  xor xor_4 (overflow, F_A_2_carry_2, Carry);
endmodule

module _3_Bit_Adder (
  input  A0,
  input  A1,
  input  A2,
  input  B0,
  input  B1,
  input  B2,
  output S0,
  output S1,
  output S2,
  output overflow,
  output Carry
);

  wire F_A_2_carry_2, F_A_carry_2;

  Full_Adder F_A (.Carry(1'b0), .X(A0), .Y(B0), .Sum(S0), .Carry_2(F_A_carry_2));
  Full_Adder F_A_2 (.Carry(F_A_carry_2), .X(A1), .Y(B1), .Sum(S1), .Carry_2(F_A_2_carry_2));
  Full_Adder F_A_3 (.Carry(F_A_2_carry_2), .X(A2), .Y(B2), .Sum(S2), .Carry_2(Carry));
  xor xor_1 (overflow, F_A_2_carry_2, Carry);
endmodule

module _3_Bit_Multiplier_v1_0 (
  input  B2,
  input  B1,
  input  B0,
  input  A2,
  input  A1,
  input  A0,
  output out_7,
  output out_8,
  output Carry,
  output M4,
  output M3,
  output M2,
  output M1,
  output M0
);

  wire and_1_out, and_2_out, and_3_out, and_4_out, and_5_out, and_6_out, and_7_out, and_8_out,
       n3_bit_adder_2_carry, n3_bit_adder_2_s1, n3_bit_adder_2_s2;

  and and_1 (and_1_out, B1, A2);
  and and_2 (and_2_out, B2, A2);
  _3_Bit_Adder u_3_bit_adder_1 (
    .A0(n3_bit_adder_2_s1), .A1(n3_bit_adder_2_s2), .A2(n3_bit_adder_2_carry), .B0(and_3_out),
    .B1(and_1_out), .B2(and_2_out), .S0(M2), .S1(M3), .S2(M4), .overflow(out_8), .Carry(Carry));
  and and_3 (and_3_out, B0, A2);
  and and_4 (and_4_out, B2, A1);
  _3_Bit_Adder u_3_bit_adder_2 (
    .A0(and_8_out), .A1(and_7_out), .A2(1'b0), .B0(and_6_out), .B1(and_5_out), .B2(and_4_out), .S0(M1),
    .S1(n3_bit_adder_2_s1), .S2(n3_bit_adder_2_s2), .overflow(out_7), .Carry(n3_bit_adder_2_carry));
  and and_5 (and_5_out, B1, A1);
  and and_6 (and_6_out, B0, A1);
  and and_7 (and_7_out, B2, A0);
  and and_8 (and_8_out, B1, A0);
  and and_9 (M0, B0, A0);
endmodule

module _3_Bit_Multiplier_v2_0 (
  input  B2,
  input  A2,
  input  B1,
  input  B0,
  input  A1,
  input  A0,
  output E_F,
  output Sign,
  output M3,
  output M2,
  output M1,
  output M0
);

  wire and_1_out, and_2_out, and_3_out, full_adder_2_carry_2;

  xor xor_1 (Sign, B2, A2);
  and and_1 (and_1_out, B1, A1);
  Full_Adder full_adder_1 (.Carry(full_adder_2_carry_2), .X(1'b0), .Y(and_1_out), .Sum(M2), .Carry_2(M3));
  and and_2 (and_2_out, B0, A1);
  and and_3 (and_3_out, B1, A0);
  Full_Adder full_adder_2 (.Carry(1'b0), .X(and_3_out), .Y(and_2_out), .Sum(M1), .Carry_2(full_adder_2_carry_2));
  and and_4 (M0, B0, A0);

  assign E_F = 1'b0;
endmodule

module _3_Bit_Multiplier_v3_0 (
  input  B2,
  input  B1,
  input  B0,
  input  A2,
  input  A1,
  input  A0,
  output Carry,
  output Overflow,
  output Sign,
  output M,
  output M2,
  output M1,
  output M0
);

  wire and_1_out, and_2_out, and_3_out, and_4_out, n3_bit_adder_1_carry, n3_bit_adder_2_carry,
       n3_bit_adder_2_s1, n3_bit_adder_2_s2, nand_1_out, nand_2_out, nand_3_out, nand_4_out;

  and and_1 (and_1_out, B2, A2);
  nand nand_1 (nand_1_out, B1, A2);
  _3_Bit_Adder u_3_bit_adder_1 (
    .A0(n3_bit_adder_2_s1), .A1(n3_bit_adder_2_s2), .A2(n3_bit_adder_2_carry), .B0(nand_3_out),
    .B1(nand_1_out), .B2(and_1_out), .S0(M2), .S1(M), .S2(Sign), .Carry(n3_bit_adder_1_carry));  // open: overflow
  xor xor_1 (Carry, 1'b1, n3_bit_adder_1_carry);
  xor xor_2 (Overflow, Carry, Sign);
  nand nand_2 (nand_2_out, B2, A1);
  _3_Bit_Adder u_3_bit_adder_2 (
    .A0(and_4_out), .A1(nand_4_out), .A2(1'b1), .B0(and_3_out), .B1(and_2_out), .B2(nand_2_out), .S0(M1),
    .S1(n3_bit_adder_2_s1), .S2(n3_bit_adder_2_s2), .Carry(n3_bit_adder_2_carry));  // open: overflow
  nand nand_3 (nand_3_out, B0, A2);
  and and_2 (and_2_out, B1, A1);
  and and_3 (and_3_out, B0, A1);
  nand nand_4 (nand_4_out, B2, A0);
  and and_4 (and_4_out, B1, A0);
  and and_5 (M0, B0, A0);
endmodule

module Full_Adder (
  input  Carry,
  input  X,
  input  Y,
  output Sum,
  output Carry_2
);

  wire and_1_out, and_2_out, xor_1_out;

  xor xor_1 (xor_1_out, X, Y);
  and and_1 (and_1_out, X, Y);
  xor xor_2 (Sum, xor_1_out, Carry);
  and and_2 (and_2_out, xor_1_out, Carry);
  or or_1 (Carry_2, and_2_out, and_1_out);
endmodule

module _3_Bit_Inverter_v1_0 (
  input  X2,
  input  X1,
  input  X0,
  output X2_2,
  output X1_2,
  output X0_2
);

  wire and_1_out, nor_1_out, nor_2_out;

  nor nor_1 (nor_1_out, X2, X1, X0);
  nor nor_2 (nor_2_out, X1, X0);
  ExactlyOne xor_1 (.out(X2_2), .in0(X2), .in1(nor_1_out), .in2(nor_2_out));
  and and_1 (and_1_out, X2, X0);
  xor xor_2 (X1_2, and_1_out, X1);

  assign X0_2 = X0;
endmodule

module _3_Bit_Inverter_v2_0 (
  input  X2,
  input  X1,
  input  X0,
  output X2_2,
  output X1_2,
  output X0_2
);

  wire and_1_out;

  and and_1 (and_1_out, X2, X0);
  xor xor_1 (X1_2, and_1_out, X1);

  assign X0_2 = X0;
  assign X2_2 = X2;
endmodule

module _2X5_Multiplexer (
  input  EFA,
  input  EFB,
  input  B4,
  input  B3,
  input  B2,
  input  B1,
  input  B0,
  input  A2,
  input  A1,
  input  A0,
  input  S0,
  output X,
  output X_2,
  output X_3,
  output X_4,
  output X_5,
  output X_6
);

  Multiplexer #(.enable("false")) multiplexer_1 (.in0(EFB), .in1(EFA), .out(X), .sel(S0));
  Multiplexer #(.enable("false")) multiplexer_2 (.in0(B4), .in1(A2), .out(X_2), .sel(S0));
  Multiplexer #(.enable("false")) multiplexer_3 (.in0(B3), .in1(1'b0), .out(X_3), .sel(S0));
  Multiplexer #(.enable("false")) multiplexer_4 (.in0(B2), .in1(1'b0), .out(X_4), .sel(S0));
  Multiplexer #(.enable("false")) multiplexer_5 (.in0(B1), .in1(A1), .out(X_5), .sel(S0));
  Multiplexer #(.enable("false")) multiplexer_6 (.in0(B0), .in1(A0), .out(X_6), .sel(S0));
endmodule
