// Logisim project Logisim File.circ as structural Verilog: 8 circuits, main circuit Main Arithmatic Unit (Mag.)
module Main (
  input  in_1,
  input  in_2,
  input  in_3,
  input  in_4,
  input  in_5,
  input  in_6,
  input  in_7,
  output out_8,
  output out_9,
  output out_10,
  output out_11,
  output out_12,
  output out_13,
  output out_14,
  output out_15,
  output out_16
);

  Main_Arithmatic_Unit__Mag main_arithmatic_unit_mag_1 (
    .B2(in_1), .B1(in_2), .B0(in_3), .A2(in_5), .A1(in_6), .A0(in_7), .X0_2(out_16), .X1_2(out_15),
    .X2(out_11), .X1(out_12), .X0(out_13), .X3(out_10), .Sign(out_9), .Sign_2(out_14), .E_F(out_8),
    .Subtraction(in_4));
endmodule

module Main_Arithmatic_Unit__Mag (
  input  Subtraction,
  input  B2,
  input  B1,
  input  B0,
  input  A2,
  input  A1,
  input  A0,
  output Sign,
  output X3,
  output X2,
  output X1,
  output X0,
  output E_F,
  output Sign_2,
  output X1_2,
  output X0_2
);

  Multiplieng_Unit multiplieng_unit_1 (
    .B2(B2), .A2(A2), .B1(B1), .B0(B0), .A1(A1), .A0(A0), .X2(X2), .X1(X1), .X0(X0), .Sign(Sign), .X3(X3));
  Add_Sub_Unit add_sub_unit_1 (
    .B2(B2), .B1(B1), .B0(B0), .A2(A2), .A1(A1), .A0(A0), .Substraction(Subtraction), .E_F(E_F),
    .Sign(Sign_2), .X1(X1_2), .X0(X0_2));
endmodule

module Add_Sub_Unit (
  input  Substraction,
  input  B2,
  input  B1,
  input  B0,
  input  A2,
  input  A1,
  input  A0,
  output E_F,
  output Sign,
  output X1,
  output X0
);

  wire _4_Bit_Adder_cout, _4_Bit_Adder_s1, _4_Bit_Adder_s2, _4_Bit_Adder_s3, and_1_out, Converter_In_x0_2,
       Converter_In_x1_2, Converter_In_x2_2, Coverter_In_x0_2, Coverter_In_x1_2, Coverter_In_x2_2, xor_1_out,
       xor_2_out, xor_3_out, xor_4_out, xor_5_out;

  xor xor_1 (xor_1_out, Converter_In_x2_2, Substraction);
  xor xor_2 (xor_2_out, xor_1_out, Coverter_In_x2_2);
  xor xor_3 (xor_3_out, xor_2_out, 1'b1);
  _3_Bit_Converter_in Converter_In (
    .X2(B2), .X1(B1), .X0(B0), .X2_2(Converter_In_x2_2), .X1_2(Converter_In_x1_2), .X0_2(Converter_In_x0_2));
  xor xor_4 (xor_4_out, Converter_In_x1_2, Substraction);
  _4_Bit_Adder _4_Bit_Adder (
    .A0(Substraction), .A1(Coverter_In_x0_2), .A2(Coverter_In_x1_2), .B0(Substraction), .B1(xor_5_out),
    .B2(xor_4_out), .S1(_4_Bit_Adder_s1), .S2(_4_Bit_Adder_s2), .Cout(_4_Bit_Adder_cout),
    .S3(_4_Bit_Adder_s3), .B2_2(xor_1_out), .A3(Coverter_In_x2_2), .Cin(1'b0));  // open: S0
  and and_1 (and_1_out, xor_3_out, _4_Bit_Adder_s3);
  or or_1 (E_F, and_1_out, _4_Bit_Adder_cout);
  xor xor_5 (xor_5_out, Converter_In_x0_2, Substraction);
  _3_Bit_Converter_out u_3_bit_converter_out_1 (
    .X2(_4_Bit_Adder_s3), .X1(_4_Bit_Adder_s2), .X0(_4_Bit_Adder_s1), .X2_2(Sign), .X1_2(X1), .X0_2(X0));
  _3_Bit_Converter_in Coverter_In (
    .X2(A2), .X1(A1), .X0(A0), .X2_2(Coverter_In_x2_2), .X1_2(Coverter_In_x1_2), .X0_2(Coverter_In_x0_2));

  // Notes on the sheet:
  //   B2 ^ A2
  //   Not
  //   OverFlow
  //   E.F = Cout + OverFlow
  //   Converter out
endmodule

module Multiplieng_Unit (
  input  B2,
  input  B1,
  input  B0,
  input  A2,
  input  A1,
  input  A0,
  output Sign,
  output X3,
  output X2,
  output X1,
  output X0
);

  wire and_1_out, and_2_out, and_3_out;

  _4_Bit_Adder u_4_bit_adder_1 (
    .A0(and_3_out), .A1(1'b0), .A2(1'b0), .B0(and_2_out), .B1(and_1_out), .B2(1'b0), .S0(X1), .S1(X2),
    .S2(X3), .S3(Sign), .B2_2(B2), .A3(A2), .Cin(1'b0));  // open: Cout
  and and_1 (and_1_out, B1, A1);
  and and_2 (and_2_out, B0, A1);
  and and_3 (and_3_out, B1, A0);
  and and_4 (X0, B0, A0);

  // Notes on the sheet:
  //   A1B0
  //   A1B1
  //   A0B1
  //   A0B0
endmodule

module _3_Bit_Converter_in (
  input  X2,
  input  X1,
  input  X0,
  output X2_2,
  output X1_2,
  output X0_2
);

  wire and_1_out, nor_1_out, nor_2_out, or_1_out, xor_2_out;

  and and_1 (and_1_out, X2, X0);
  nor nor_1 (nor_1_out, X1, X0);
  or or_1 (or_1_out, X1, X0);
  xor xor_1 (X1_2, and_1_out, X1);
  xor xor_2 (xor_2_out, X2, nor_1_out);
  nor nor_2 (nor_2_out, or_1_out, X2);
  xor xor_3 (X2_2, xor_2_out, nor_2_out);

  assign X0_2 = X0;
endmodule

module _3_Bit_Converter_out (
  input  X2,
  input  X1,
  input  X0,
  output X2_2,
  output X1_2,
  output X0_2
);

  wire and_1_out;

  and and_1 (and_1_out, X2, X0);
  xor xor_1 (X1_2, and_1_out, X1);

  assign X0_2 = X0;
  assign X2_2 = X2;
endmodule

module _4_Bit_Adder (
  input  Cin,
  input  A0,
  input  A1,
  input  A2,
  input  A3,
  input  B0,
  input  B1,
  input  B2,
  input  B2_2,
  output S0,
  output S1,
  output S2,
  output S3,
  output Cout
);

  wire F_A_2_carry_2, F_A_3_carry_2, F_A_carry_2;

  Full_Adder F_A (.Carry(Cin), .X(A0), .Y(B0), .Sum(S0), .Carry_2(F_A_carry_2));
  Full_Adder F_A_2 (.Carry(F_A_carry_2), .X(A1), .Y(B1), .Sum(S1), .Carry_2(F_A_2_carry_2));
  Full_Adder F_A_3 (.Carry(F_A_2_carry_2), .X(A2), .Y(B2), .Sum(S2), .Carry_2(F_A_3_carry_2));
  Full_Adder F_A_4 (.Carry(F_A_3_carry_2), .X(A3), .Y(B2_2), .Sum(S3), .Carry_2(Cout));
endmodule

module Full_Adder (
  input  Carry,
  input  X,
  input  Y,
  output Sum,
  output Carry_2
);

  wire and_1_out, and_2_out, xor_1_out;

  xor xor_1 (xor_1_out, X, Y);
  and and_1 (and_1_out, X, Y);
  xor xor_2 (Sum, xor_1_out, Carry);
  and and_2 (and_2_out, xor_1_out, Carry);
  or or_1 (Carry_2, and_2_out, and_1_out);
endmodule
